# Fritzing sketch Remote-blink (saved by Fritzing 0.9.3b)
breadboards: 1

parts:
  Part1 = Arduino Uno (Rev3)
  U1 = ESP8266 WiFi Module [part_number=ESP8266]

nets:
  N1: Part1.D2, U1.TXD
  N2: Part1.D3_PWM, U1.RXD, U1.GPIO_0
  3V3: Part1.3V3, U1.VCC, U1.RST, U1.CH_PD
  GND: Part1.GND, U1.GND

custom parts:
  ESP8266 WiFi Module: Generic WiFi Module based on the ESP8266 with onboard PCB antenna and UART communications
